# Fritzing sketch LedRGBRaspberryPi (saved by Fritzing 0.9.2b)
circuit board: 3.52073cm x 1.72861cm
breadboards: 1

parts:
  Raspberry_Pi_B_rev1 = Raspberry Pi B rev1
  LED_RGB = RGB LED (com. cathode, rgb) [package="5 mm [THT]"]
  R1 = Resistor [tolerance=±5% resistance=220 package=THT]
  R2 = Resistor [tolerance=±5% resistance=220 package=THT]
  R3 = Resistor [tolerance=±5% resistance=220 package=THT]
  J2 = double row female pin header, 26 pins [form="♀ (female)"]  # not connected

nets:
  GND: Raspberry_Pi_B_rev1.GND, LED_RGB.common_cathode
  N1: Raspberry_Pi_B_rev1.GPIO_23, Raspberry_Pi_B_rev1.GPIO_21, R1.Pin_0, R2.Pin_1
  N2: Raspberry_Pi_B_rev1.GPIO_25, R3.Pin_1
  N3: LED_RGB.red_anode, R3.Pin_0
  N4: LED_RGB.green_anode, LED_RGB.blue_anode, R1.Pin_1, R2.Pin_0
